# Fritzing sketch breadboard (saved by Fritzing 1.0.1rc)
breadboards: 1

parts:
  Mod1 = CRV1D0512SC [package=THT]
  Mod2 = Raspberry Pi Pico
  IC1 = Dual Op-Amp [package=dip08]
  C1 = Ceramic Capacitor [capacitance=100nF voltage=35V package="100 mil [THT, multilayer]"]
  C2 = Tantalum Capacitor [capacitance=1μF voltage=35V package="100 mil [THT, tantalum]"]
  C3 = Tantalum Capacitor [capacitance=1μF voltage=35V package="100 mil [THT, tantalum]"]
  C4 = Ceramic Capacitor [capacitance="100 nF" voltage=35V package="0805 [SMD, multilayer]"]
  C5 = Ceramic Capacitor [capacitance=100nF voltage=35V package="100 mil [THT, multilayer]"]
  C6 = Tantalum Capacitor [capacitance=1μF voltage=35V package="100 mil [THT, tantalum]"]
  C7 = Ceramic Capacitor [capacitance=100nF voltage=35V package="100 mil [THT, multilayer]"]
  C8 = Ceramic Capacitor [capacitance=100nF voltage=35V package="100 mil [THT, multilayer]"]
  R1 = Resistor [tolerance=±5% resistance=220 package="2010 [SMD]"]
  R2 = Resistor [tolerance=±5% resistance=220 package="2010 [SMD]"]
  R3 = Resistor [tolerance=±5% resistance=220 package="2010 [SMD]"]
  R4 = Resistor [tolerance=±5% resistance=220 package="2010 [SMD]"]
  C9 = Ceramic Capacitor [capacitance=100nF voltage=35V package="100 mil [THT, multilayer]"]
  U1 = BNC [package=bnc]

nets:
  N1: Mod1.Vin, Mod2.pin_40, C5.0, C6.+
  GND: Mod1.Gnd, Mod1.0V, Mod2.pin_3, Mod2.pin_8, Mod2.pin_13, Mod2.pin_18, Mod2.pin_23, Mod2.pin_28, Mod2.pin_33, Mod2.pin_38, C1.1, C2.-, C3.+, C4.0, C5.1, C6.-, C7.1, C9.0, U1.GND
  N2: Mod1.-Vout, IC1.A_V-, C3.-, C4.1
  N3: Mod1.+Vout, C1.0, C2.+
  N4: Mod2.pin_9, R2.Pin_0
  N5: Mod2.pin_14, R1.Pin_0
  N6: IC1.A_OUT, C8.1, R4.Pin_0, U1.OUT
  N7: IC1.A_-IN, C8.0, R3.Pin_1
  N8: IC1.A_+IN, C7.0, R1.Pin_1
  N9: R2.Pin_1, R3.Pin_0, R4.Pin_1, C9.1

custom parts:
  CRV1D0512SC: Murata CRV1D0512SC 1W, fixed input isolated and unregulated dual output miniature sip package
  Raspberry Pi Pico: Raspberry Pi Pico. Based around the RP2040 microcontroller the Pico is a low cost microcontroller device bringing Raspberry Pi quality, cost, and easy of use to the microcontroller space. Jan 2021, Split part in to two versions: tht (this one) and SMD. This one will drill holes for a .1 in header in pcb to allow plugging in the module as well as providing pads to solder the module to the top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
